# Fritzing sketch teensy_board (saved by Fritzing 0.9.3b)

parts:
  A1 = Teensy 4.0
  R1 = Resistor [tolerance=±5% resistance=10k package="0603 [SMD]"]
  R2 = Resistor [tolerance=±5% resistance=10k package="0603 [SMD]"]
  R3 = Resistor [tolerance=±5% resistance=10k package="0603 [SMD]"]
  R4 = Resistor [tolerance=±5% resistance=10k package="0603 [SMD]"]
  R5 = Resistor [tolerance=±5% resistance=10k package="0603 [SMD]"]
  R6 = Resistor [tolerance=±5% resistance=10k package="0603 [SMD]"]
  R7 = Resistor [tolerance=±5% resistance=10k package="0603 [SMD]"]
  R8 = Resistor [tolerance=±5% resistance=10k package="0603 [SMD]"]
  R9 = Resistor [tolerance=±5% resistance=10k package="0603 [SMD]"]
  R10 = Resistor [tolerance=±5% resistance=10k package="0603 [SMD]"]
  R11 = Resistor [tolerance=±5% resistance=10k package="0603 [SMD]"]
  R12 = Resistor [tolerance=±5% resistance=10k package="0603 [SMD]"]
  R13 = Resistor [tolerance=±5% resistance=10k package="0603 [SMD]"]
  R14 = Resistor [tolerance=±5% resistance=10k package="0603 [SMD]"]
  R15 = Resistor [tolerance=±5% resistance=10k package="0603 [SMD]"]
  W5500_Module1 = W5500 Ethernet module [package="DIP (Dual Inline) [THT]"]

nets:
  N1: A1.pin_1, A1.pin_17, A1.pin_32, R2.Pin_0, R6.Pin_0, R9.Pin_0, R11.Pin_1, R15.Pin_1, W5500_Module1.GND
  N2: A1.pin_2, R10.Pin_0
  N3: A1.pin_9, R13.Pin_0
  N4: A1.pin_12, W5500_Module1.SCS
  N5: A1.pin_13, W5500_Module1.MOSI
  N6: A1.pin_14, W5500_Module1.MISO
  N7: A1.pin_16, A1.pin_31, W5500_Module1.3.3V
  N8: A1.pin_20, W5500_Module1.SCLK
  N9: A1.pin_22, R7.Pin_1
  N10: A1.pin_23, R4.Pin_1
  N11: A1.pin_28, R3.Pin_1
  N12: R1.Pin_0, R2.Pin_1
  N13: R5.Pin_0, R6.Pin_1
  N14: R8.Pin_0, R9.Pin_1
  N15: R11.Pin_0, R12.Pin_1
  N16: R14.Pin_1, R15.Pin_0

custom parts:
  Teensy 4.0: The Teensy is a complete USB-based microcontoller development system, in a very small footprint, capable of implementing many types of projects. All programming is done via the USB port. No special programmer is needed, only a standard micro-USB cable and a PC or Macintosh with a USB port. (Oct 2023 added the VBUS pad at user request.)
  W5500 Ethernet module: W5500 based SPI Ethernet module for Arduino, etc.
