# Fritzing sketch Redesign component board 1.0 (saved by Fritzing 0.9.3b)

parts:
  Pro_micro = Arduino Pro Mini (5V)
  U2 = MCP23017 [package=dil28-3]
  U3 = MCP23017 [package=dil28-3]
  U4 = MCP23017 [package=dil28-3]  # not connected

nets:
  N1: Pro_micro.D9, U2.INTA
  N2: Pro_micro.D8, U3.INTA
  N3: Pro_micro.D3, U2.SDA, U3.SDA
  N4: Pro_micro.D2, U2.SCL, U3.SCL

notes:
  Bruin is data lines
  Boven is scl
  onder is scl
  op pro micro is dat andersom
  Gnd serial|serial poort| serial poort | vcc | gnd sensoren, mcp| extra| gnd led | led| led|

custom parts:
  MCP23017: 16 bit I/O chip controlled via I2C
